// Logisim project mappages_tp1.circ as structural Verilog: 6 circuits, main circuit main
module main (
  input  mja,
  input  mjb,
  input  mjc,
  input  a,
  input  b,
  input  sel,
  output mjout,
  output normal,
  output o,
  output perso
);

  Multiplexer multiplexer_1 (.in0(a), .in1(b), .out(normal), .sel(sel));
  MX2_1 MX2_1_1 (.s(sel), .a(a), .b(b), .o(perso));
  maj3 maj3_1 (.c(mja), .a(mjb), .b(mjc), .o(mjout));
  xnor xnor_1 (o, normal, perso);

  // Other names for the same wires on the sheet: s = sel
endmodule

module Tst (
  input  a,
  input  b,
  input  s,
  output out_4
);

  wire and_1_out, and_2_out, multiplexer_1_out, or_1_out;

  and and_1 (and_1_out, ~s, a);  // AND_Gate
  and and_2 (and_2_out, s, b);
  or or_1 (or_1_out, and_1_out, and_2_out);
  Multiplexer multiplexer_1 (.in0(a), .in1(b), .out(multiplexer_1_out), .sel(s));
  xor xor_1 (out_4, or_1_out, multiplexer_1_out);
endmodule

module MX2_1 (
  input  s,
  input  a,
  input  b,
  output o
);

  wire and_1_out, and_2_out, not_1_out;

  not not_1 (not_1_out, s);
  and and_1 (and_1_out, not_1_out, a);
  or or_1 (o, and_1_out, and_2_out);
  and and_2 (and_2_out, s, b);
endmodule

module maj3 (
  input  c,
  input  a,
  input  b,
  output o
);

  wire and_1_out, and_2_out, and_3_out;

  and and_1 (and_1_out, a, b);
  and and_2 (and_2_out, c, b);
  or or_1 (o, and_1_out, and_2_out, and_3_out);
  and and_3 (and_3_out, c, a);
endmodule

module demux4 (
  input  i,
  input  [1:0] sel,
  output O0,
  output O1,
  output O2,
  output O3
);

  wire and_1_out, and_2_out, and_3_out, and_4_out;

  and and_1 (and_1_out, ~sel[0], ~sel[1]);  // AND_Gate
  and and_2 (and_2_out, sel[0], ~sel[1]);  // AND_Gate
  and and_3 (and_3_out, ~sel[0], sel[1]);  // AND_Gate
  and and_4 (and_4_out, sel[0], sel[1]);
  and and_5 (O0, i, and_1_out);
  and and_6 (O1, i, and_2_out);
  and and_7 (O2, i, and_3_out);
  and and_8 (O3, i, and_4_out);

  // Other names for the same wires on the sheet: s0 = sel[0]; s1 = sel[1]
endmodule

module vu_metre_LED (
  input  [2:0] inp,
  input  M_A,
  output l7,
  output l6,
  output l5,
  output l4,
  output l3,
  output l2,
  output l1,
  output l0
);

  wire inp0, inp1, inp2;

  or or_1 (l0, inp2, inp1, inp0);
  Multiplexer #(.width(3)) multiplexer_1 (.in0(3'b000), .in1(inp), .out({inp2, inp1, inp0}), .sel(M_A));
  or or_2 (l1, inp2, inp1);
endmodule
